// Logisim project hw3.circ as structural Verilog: 5 circuits, main circuit 16-bit ALU
module _1_bit_full_adder (
  input  A,
  input  B,
  input  CarryIn,
  output Answer,
  output CarryOut
);

  wire and_1_out, and_2_out, and_3_out, and_4_out, and_5_out, and_6_out, and_7_out;

  and and_1 (and_1_out, ~A, ~B, CarryIn);  // AND_Gate
  and and_2 (and_2_out, A, ~B, ~CarryIn);  // AND_Gate
  and and_3 (and_3_out, A, B, CarryIn);
  and and_4 (and_4_out, ~A, B, ~CarryIn);  // AND_Gate
  and and_5 (and_5_out, A, ~B, CarryIn);  // AND_Gate
  and and_6 (and_6_out, B, CarryIn);
  and and_7 (and_7_out, A, B, ~CarryIn);  // AND_Gate
  or or_1 (Answer, and_1_out, and_2_out, and_3_out, and_4_out);
  or or_2 (CarryOut, and_5_out, and_6_out, and_7_out);

  // Notes on the sheet:
  //   Stephanie Remy    GTID: 902776472
endmodule

module _4_bit_full_adder (
  input  [3:0] A,
  input  [3:0] B,
  input  CarryIn,
  output [3:0] Answer,
  output CarryOut
);

  wire n1_bit_full_adder_1_carryout, n1_bit_full_adder_2_carryout, n1_bit_full_adder_3_carryout;

  _1_bit_full_adder u_1_bit_full_adder_1 (
    .A(A[0]), .B(B[0]), .CarryIn(CarryIn), .Answer(Answer[0]), .CarryOut(n1_bit_full_adder_1_carryout));
  _1_bit_full_adder u_1_bit_full_adder_2 (
    .A(A[1]), .B(B[1]), .CarryIn(n1_bit_full_adder_1_carryout), .Answer(Answer[1]),
    .CarryOut(n1_bit_full_adder_2_carryout));
  _1_bit_full_adder u_1_bit_full_adder_3 (
    .A(A[2]), .B(B[2]), .CarryIn(n1_bit_full_adder_2_carryout), .Answer(Answer[2]),
    .CarryOut(n1_bit_full_adder_3_carryout));
  _1_bit_full_adder u_1_bit_full_adder_4 (
    .A(A[3]), .B(B[3]), .CarryIn(n1_bit_full_adder_3_carryout), .Answer(Answer[3]), .CarryOut(CarryOut));

  // Notes on the sheet:
  //   Stephanie Remy GTID: 902776472
endmodule

module _4_bit_ALU (
  input  [3:0] A,
  input  [3:0] B,
  input  S0,
  input  S2,
  input  S1,
  output [3:0] Answer,
  output out_7,
  output out_8,
  output out_9,
  output out_10
);

  wire [3:0] and_1_out, n4_bit_full_adder_1_answer, n4_bit_full_adder_2_answer, n4_bit_full_adder_3_answer,
       n4_bit_full_adder_4_answer, not_1_out, not_5_out, or_1_out, xor_1_out;

  not not_1 (not_1_out[0], B[0]);
  not not_2 (not_1_out[1], B[1]);
  not not_3 (not_1_out[2], B[2]);
  not not_4 (not_1_out[3], B[3]);
  assign and_1_out = A & B;  // AND_Gate and_1, 4 bits wide
  assign or_1_out = A | B;  // OR_Gate or_1, 4 bits wide
  assign xor_1_out = A ^ B;  // XOR_Gate xor_1, 4 bits wide
  _4_bit_full_adder u_4_bit_full_adder_1 (
    .A(A), .B(B), .CarryIn(1'b0), .Answer(n4_bit_full_adder_1_answer));  // open: CarryOut
  _4_bit_full_adder u_4_bit_full_adder_2 (
    .A(not_1_out), .B(4'b0001), .CarryIn(1'b0), .Answer(n4_bit_full_adder_2_answer));  // open: CarryOut
  not not_5 (not_5_out[0], A[0]);
  not not_6 (not_5_out[1], A[1]);
  not not_7 (not_5_out[2], A[2]);
  not not_8 (not_5_out[3], A[3]);
  _4_bit_full_adder u_4_bit_full_adder_3 (
    .A(A), .B(n4_bit_full_adder_2_answer), .CarryIn(1'b0), .Answer(n4_bit_full_adder_3_answer));  // open: CarryOut
  _4_bit_full_adder u_4_bit_full_adder_4 (
    .A(not_5_out), .B(4'b0001), .CarryIn(1'b0), .Answer(n4_bit_full_adder_4_answer));  // open: CarryOut
  Multiplexer #(.select(3), .width(4), .disabled(0), .enable("false")) multiplexer_1 (
    .in0(n4_bit_full_adder_1_answer), .in1(n4_bit_full_adder_3_answer), .in2({3'b000, A[0]}),
    .in3(n4_bit_full_adder_4_answer), .in4({A[2:0], 1'b0}), .in5(and_1_out), .in6(or_1_out), .in7(xor_1_out),
    .out(Answer), .sel({S2, S1, S0}));

  assign out_7 = A[1];
  assign out_8 = A[2];
  assign out_9 = A[3];
  assign out_10 = A[3];

  // Notes on the sheet:
  //   Substraction
  //   IsOddNumber
  //   Negation
  //   Multiply by 2
  //   Stephanie Remy   GTID: 902776472
  //   Addition
  //   OR
  //   AND
  //   XOR
  //   (Operation)
  //   Addition   000
  //   Subtraction    001
  //   IsOddNumber  010
  //   Negation   011
  //   Multiply by 2    100
  //   AND    101
  //   OR   110
  //   XOR    111
  //   (S2, S1, S0)
endmodule

module _16_bit_ALU (
  input  S0,
  input  S1,
  input  S2,
  input  [15:0] A,
  input  [15:0] B,
  output [15:0] out_6,
  output [14:0] out_7,
  output AND
);

  wire [15:0] and_1_out, n16_bit_adder_1_output, n16_bit_adder_2_output, n16_bit_adder_3_output,
       n16_bit_adder_4_output, not_1_out, not_2_out, or_1_out, xor_1_out;

  assign not_1_out = ~B;  // NOT_Gate not_1, 16 bits wide
  _16_bit_adder u_16_bit_adder_1 (
    .A(not_2_out), .B(16'h1), .CarryIn(1'b0), .Output(n16_bit_adder_1_output));  // open: CarryOut
  assign not_2_out = ~A;  // NOT_Gate not_2, 16 bits wide
  _16_bit_adder u_16_bit_adder_2 (.A(A), .B(B), .CarryIn(1'b0), .Output(n16_bit_adder_2_output));  // open: CarryOut
  _16_bit_adder u_16_bit_adder_3 (
    .A(A), .B(n16_bit_adder_4_output), .CarryIn(1'b0), .Output(n16_bit_adder_3_output));  // open: CarryOut
  _16_bit_adder u_16_bit_adder_4 (
    .A(not_1_out), .B(16'h1), .CarryIn(1'b0), .Output(n16_bit_adder_4_output));  // open: CarryOut
  assign and_1_out = A & B;  // AND_Gate and_1, 16 bits wide
  assign or_1_out = A | B;  // OR_Gate or_1, 16 bits wide
  assign xor_1_out = A ^ B;  // XOR_Gate xor_1, 16 bits wide
  Multiplexer #(.select(3), .width(16), .disabled(0), .enable("false")) multiplexer_1 (
    .in0(n16_bit_adder_2_output), .in1(n16_bit_adder_3_output), .in2({{15{1'b0}}, A[0]}),
    .in3(n16_bit_adder_1_output), .in4({A[14:0], 1'b0}), .in5(and_1_out), .in6(or_1_out), .in7(xor_1_out),
    .out(out_6), .sel({S2, S1, S0}));

  assign AND = A[15];
  assign out_7 = A[15:1];

  // Other names for the same wires on the sheet: Answer[15:0] = out_6; Selection[2:0] = {S2, S1, S0}

  // Notes on the sheet:
  //   Stephanie Remy    GTID: 902776472
  //   Addition
  //   Negation
  //   Multipy By 2
  //   IsOddNumber
  //   OR
  //   XOR
  //   Subtraction
  //   (Operation)     (S2, S1, S0)
  //   Addition   000
  //   Subtraction    001
  //   IsOddNumber    010
  //   Negation   011
  //   Multiply by 2    100
  //   AND    101
  //   OR   110
  //   XOR    111
endmodule

module _16_bit_adder (
  input  [15:0] A,
  input  [15:0] B,
  input  CarryIn,
  output [15:0] Output,
  output CarryOut
);

  wire n4_bit_full_adder_1_carryout, n4_bit_full_adder_2_carryout, n4_bit_full_adder_3_carryout;

  _4_bit_full_adder u_4_bit_full_adder_1 (
    .A(A[3:0]), .B(B[3:0]), .CarryIn(CarryIn), .Answer(Output[3:0]), .CarryOut(n4_bit_full_adder_1_carryout));
  _4_bit_full_adder u_4_bit_full_adder_2 (
    .A(A[7:4]), .B(B[7:4]), .CarryIn(n4_bit_full_adder_1_carryout), .Answer(Output[7:4]),
    .CarryOut(n4_bit_full_adder_2_carryout));
  _4_bit_full_adder u_4_bit_full_adder_3 (
    .A(A[11:8]), .B(B[11:8]), .CarryIn(n4_bit_full_adder_2_carryout), .Answer(Output[11:8]),
    .CarryOut(n4_bit_full_adder_3_carryout));
  _4_bit_full_adder u_4_bit_full_adder_4 (
    .A(A[15:12]), .B(B[15:12]), .CarryIn(n4_bit_full_adder_3_carryout), .Answer(Output[15:12]),
    .CarryOut(CarryOut));

  // Notes on the sheet:
  //   Stephanie Remy   GTID: 902776472
endmodule
