// Logisim project xor.circ as structural Verilog: 1 circuit, main circuit my circuit
module my_circuit (
  input  x,
  input  y,
  output x_XOR_y
);

  wire and_1_out, and_2_out, not_1_out, not_2_out;

  not not_1 (not_1_out, x);
  not not_2 (not_2_out, y);
  and and_1 (and_1_out, not_1_out, y);
  and and_2 (and_2_out, x, not_2_out);
  or or_1 (x_XOR_y, and_1_out, and_2_out);

  // Notes on the sheet:
  //   Stephanie Remy
  //   GTID: 902776472   Jan 14th, 2016   XOR Circuit
endmodule
